# Fritzing sketch SemTempoIrmao (saved by Fritzing 0.9.3b)
breadboards: 3

parts:
  Componente1 = Arduino Mega 2560 (Rev3)
  Componente3 = 2.4 Touchscreen TFT Breakout w:MicroSD
  hc-sr1 = hc-sr04
  R1 = PHOTOCELL [package=photocell]
  R2 = Resistor [tolerance=±5% resistance=220 package="2010 [SMD]"]
  R3 = Resistor [tolerance=±5% resistance=220 package="2010 [SMD]"]
  R4 = Resistor [tolerance=±5% resistance=220 package="2010 [SMD]"]
  J1 = Piezo Speaker
  S1 = Pushbutton [package="[SMD]"]
  R5 = Resistor [tolerance=±5% resistance=220 package="2010 [SMD]"]
  S2 = Pushbutton [package="[SMD]"]
  S3 = Pushbutton [package="[SMD]"]
  S4 = Pushbutton [package="[SMD]"]
  R6 = Resistor [tolerance=±5% resistance=220 package="2010 [SMD]"]
  R7 = Resistor [tolerance=±5% resistance=220 package="2010 [SMD]"]
  R8 = Resistor [tolerance=±5% resistance=220 package="2010 [SMD]"]
  LED1 = smd LED [color="Red (633nm)" package="1206 [SMD]"]
  LED2 = smd LED [color="Yellow (595nm)" package="1206 [SMD]"]
  LED3 = smd LED [color="Green (570nm)" package="1206 [SMD]"]
  R9 = Resistor [tolerance=±5% resistance=220 package="2010 [SMD]"]
  R10 = Resistor [tolerance=±5% resistance=220 package="2010 [SMD]"]
  R11 = Resistor [tolerance=±5% resistance=220 package="2010 [SMD]"]

nets:
  N1: Componente1.A14, R1.P$2, R2.Pin_0
  N2: Componente1.A0, Componente3.X-
  N3: Componente1.A1, Componente3.IM0
  N4: Componente1.A2, Componente3.IM1
  N5: Componente1.A3, Componente3.IM2
  N6: Componente1.A4, Componente3.IM3
  N7: Componente1.A5, Componente3.SD_CS
  N8: Componente1.A6, Componente3.CARDDET
  N9: Componente1.IOREF#254, Componente3.MISO
  N10: Componente1.IOREF#255, Componente3.MOSI
  N11: Componente1.RESET, Componente3.CS
  N12: Componente1.3V3, Componente3.WR_DC
  5V: Componente1.5V, Componente3.RST, hc-sr1.VCC, R1.P$1, R3.Pin_1, S1.Pin_3, S1.Pin_4, S2.Pin_2, S3.Pin_1, S3.Pin_2, S4.Pin_2
  GND: Componente1.GND, Componente3.LITE, Componente3.Y+, hc-sr1.GND, R2.Pin_1, R4.Pin_0, J1.pin1, R5.Pin_1, R6.Pin_0, R7.Pin_0, R8.Pin_0, R9.Pin_1, R10.Pin_1, R11.Pin_1
  N13: Componente1.VIN, Componente3.X+
  N14: Componente1.D0_RX0, Componente3.D6
  N15: Componente1.D1_TX0, Componente3.D5
  N16: Componente1.D2_PWM, Componente3.D4
  N17: Componente1.D3_PWM, Componente3.D3
  N18: Componente1.D4_PWM, Componente3.D2
  N19: Componente1.D5_PWM, Componente3.D1
  N20: Componente1.D6_PWM, Componente3.D0
  N21: Componente1.D7_PWM, Componente3.Y-
  N22: Componente1.D22, LED1.cathode
  N23: Componente1.D23, S4.Pin_3, S4.Pin_4, R8.Pin_1
  N24: Componente1.D24, LED2.cathode
  N25: Componente1.D25, S3.Pin_3, S3.Pin_4, R6.Pin_1
  N26: Componente1.D26, LED3.cathode
  N27: Componente1.D27, S2.Pin_3, S2.Pin_4, R7.Pin_1
  N28: Componente1.D36, S1.Pin_1, S1.Pin_2, R5.Pin_0
  N29: Componente1.D39, hc-sr1.Trig
  N30: Componente1.D41, hc-sr1.Echo
  N31: Componente1.D52, J1.pin2
  N32: R3.Pin_0, R4.Pin_1
  N33: LED1.anode, R9.Pin_0
  N34: LED2.anode, R10.Pin_0
  N35: LED3.anode, R11.Pin_0

custom parts:
  2.4 Touchscreen TFT Breakout w:MicroSD: Add some jazz & pizzazz to your project with a color touchscreen LCD. This TFT display is 2.4" diagonal with a bright (4 white-LED) backlight and it's colorful! 240x320 pixels with individual RGB pixel control, this has way more resolution than a black and white 128x64 display. As a bonus, this display has a resistive touchscreen attached to it already, so you can detect finger presses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
